# Fritzing sketch curtain_control_scheme (saved by Fritzing 0.9.3b)
breadboards: 1

parts:
  U1 = NodeMCU V3.0
  12v_to_5v_step_down = RioRand LM2596
  Power_supply = Power plug [part_number=12v]
  0_68V = Pololu A4988 [package=SO16]
  17HS4401 = Stepper Motor - Bipolar
  R1 = Resistor [tolerance=±5% resistance=100k package="2010 [SMD]"]
  100uf = Capacitor Polarized [package=cpol-radial-100uf-25v]

nets:
  N1: U1.D1, 0_68V.ENABLE
  N2: U1.D2, 0_68V.SLEEP
  GND: U1.GND#6, U1.GND#13, U1.GND#16, U1.GND#33, 12v_to_5v_step_down.Pin_2, 12v_to_5v_step_down.Pin_4, Power_supply.GND, 0_68V.GND, 100uf.-
  N3: U1.D5, 0_68V.DIR
  N4: U1.D6, 0_68V.STEP
  N5: U1.D7, 0_68V.MS1
  N6: U1.D8, 0_68V.MS2
  VIN: U1.Vin, 12v_to_5v_step_down.Pin_3, 0_68V.VDD, R1.Pin_0
  N7: 12v_to_5v_step_down.Pin_1, Power_supply.VCC, 0_68V.VMOT, 100uf.+
  N8: 0_68V.RESET, R1.Pin_1
  N9: 0_68V.1B, 17HS4401.D
  N10: 0_68V.1A, 17HS4401.B
  N11: 0_68V.2A, 17HS4401.C
  N12: 0_68V.2B, 17HS4401.A

notes:
  12v
  5v

custom parts:
  NodeMCU V3.0: ESP8266 based NodeMCU
