# Fritzing sketch esp01_arduino (saved by Fritzing 0.9.3b)
breadboards: 1

parts:
  Power_supply = Power plug [part_number=220v]
  470uf = Capacitor Polarized [package=cpol-radial-100uf-25v]
  HLK-PM1 = HLK-PM01
  esp01_with_relay = RELAY [package=relay-g5q]
  2N3904 = NPN-Transistor [package="TO92 [THT]"]
  LED1 = LED - 3mm [color="Infrared (940nm)" package="3 mm [THT]"]
  Lamp_220v = LEDs [package=led10mm]
  R2 = Resistor [tolerance=±5% resistance=1k package="2010 [SMD]"]
  HW-484 = Breakout Board for Electret Microphone
  DHT-11 = Humidity and Temperature Sensor RHT03
  R3 = Resistor [tolerance=±5% resistance=10k package="2010 [SMD]"]
  5V_to_3_3V_board = ESP8266 WiFi Module
  Часть1 = Arduino Nano (Rev3.0)
  R4 = Resistor [tolerance=±5% resistance=1k package="2010 [SMD]"]
  R5 = Resistor [tolerance=±5% resistance=2 package="2010 [SMD]"]

nets:
  N1: Power_supply.GND, HLK-PM1.AC#1
  N2: Power_supply.VCC, HLK-PM1.AC#0, Lamp_220v.C
  VCC: 470uf.+, HLK-PM1.+Vo, LED1.anode, HW-484.VCC, DHT-11.Vcc, Часть1.VIN
  GND: 470uf.-, HLK-PM1.-Vo, 2N3904.C, HW-484.GND, DHT-11.GND_2, Часть1.GND, R5.Pin_1
  N3: esp01_with_relay.NO, Lamp_220v.A
  N4: 2N3904.E, LED1.cathode
  N5: 2N3904.B, R2.Pin_1
  N6: R2.Pin_0, Часть1.D3
  N7: HW-484.AUD, Часть1.D11/MOSI
  N8: DHT-11.Data-signal, R3.Pin_0, Часть1.D12/MISO
  N9: 5V_to_3_3V_board.RXD, R4.Pin_1, R5.Pin_0
  N10: 5V_to_3_3V_board.TXD, Часть1.D0/RX
  N11: Часть1.D1/TX, R4.Pin_0

custom parts:
  ESP8266 WiFi Module: Generic WiFi Module based on the ESP8266 with onboard PCB antenna and UART communications
