# Fritzing sketch led_bathroom (saved by Fritzing 0.9.3b)
breadboards: 2

parts:
  U1 = NodeMCU V3.0
  M1 = RioRand LM2596
  Power_supply_12v_5A = Power plug
  IRFZ44N_x3_parallel = Basic FET N-Channel [package="TO220 [THT]"]
  HC-SR501 = LHi958 [package=to-39]
  LED2 = LED - 5mm [color="Red (633nm)" package="5 mm [THT]"]
  HC-SR501_2 = LHi958 [package=to-39]
  470uf = Capacitor Polarized [package=cpol-radial-100uf-25v]
  470uf_2 = Capacitor Polarized [package=cpol-radial-100uf-25v]
  470uf_3 = Capacitor Polarized [package=cpol-radial-100uf-25v]
  2N2222 = NPN-Transistor [package="TO92 [THT]"]
  U2 = mystery part, 2 pins [chip_label=FAN]
  R3 = Resistor [tolerance=±5% resistance=1k package="2010 [SMD]"]
  DHT-11 = Humidity and Temperature Sensor RHT03
  R4 = Resistor [tolerance=±5% resistance=10k package="2010 [SMD]"]
  3144_B8211 = HALL-EFFECT [package=sc70]
  R5 = Resistor [tolerance=±5% resistance=10k package="2010 [SMD]"]
  IRFZ44N1 = Basic FET N-Channel [package="TO220 [THT]"]
  IRFZ44N2 = Basic FET N-Channel [package="TO220 [THT]"]
  R6 = Resistor [tolerance=±5% resistance=10k package="2010 [SMD]"]

nets:
  N1: U1.D1, HC-SR501.S
  N2: U1.D2, HC-SR501_2.S
  N3: U1.D3, DHT-11.Data-signal, R4.Pin_0
  N4: U1.D4, R5.Pin_0
  3V3: U1.3V3, 470uf_3.+, DHT-11.Vcc, R4.Pin_1, R5.Pin_1
  GND: U1.GND#6, U1.GND#13, U1.GND#16, U1.GND#33, M1.Pin_2, M1.Pin_4, Power_supply_12v_5A.GND, IRFZ44N_x3_parallel.source, HC-SR501.GND, HC-SR501_2.GND, 470uf.-, 470uf_2.-, 470uf_3.-, 2N2222.C, DHT-11.GND_2, 3144_B8211.GND, IRFZ44N1.source, IRFZ44N2.source, R6.Pin_0
  N5: U1.D6, IRFZ44N_x3_parallel.gate, IRFZ44N1.gate, IRFZ44N2.gate, R6.Pin_1
  N6: U1.D7, R3.Pin_0
  N7: U1.Vin, M1.Pin_3, HC-SR501.D, HC-SR501_2.D, 470uf_2.+
  N8: M1.Pin_1, Power_supply_12v_5A.VCC, LED2.anode, 470uf.+, U2.pin1
  N9: IRFZ44N_x3_parallel.drain, LED2.cathode, IRFZ44N1.drain, IRFZ44N2.drain
  N10: 2N2222.E, U2.pin2
  N11: 2N2222.B, R3.Pin_1

notes:
  12v
  5v
  led strip2 12v
  3.3v

custom parts:
  NodeMCU V3.0: ESP8266 based NodeMCU
