# Fritzing sketch irsend_soundsensor_temp_scheme (saved by Fritzing 0.9.3b)
breadboards: 1

parts:
  U1 = NodeMCU V3.0
  Power_supply = Power plug [part_number=220v]
  R1 = Resistor [tolerance=±5% resistance=1k package="2010 [SMD]"]
  470uf = Capacitor Polarized [package=cpol-radial-100uf-25v]
  HLK-PM1 = HLK-PM01
  5v_relay = RELAY [package=relay-g5q]
  2N3904 = NPN-Transistor [package="TO92 [THT]"]
  2N3904_2 = NPN-Transistor [package="TO92 [THT]"]
  part = LED - 3mm [color="Infrared (940nm)" package="3 mm [THT]"]
  Lamp_220v = LEDs [package=led10mm]
  R2 = Resistor [tolerance=±5% resistance=1k package="2010 [SMD]"]
  HW-484 = Breakout Board for Electret Microphone
  diode = Schottky Diode [part_number="cathode to plus" package="300 mil [THT]"]
  DHT-11 = Humidity and Temperature Sensor RHT03
  R3 = Resistor [tolerance=±5% resistance=10k package="2010 [SMD]"]

nets:
  N1: U1.D1, R2.Pin_0
  N2: U1.D2, R1.Pin_0
  VCC: U1.3V3, part.anode, HW-484.VCC, DHT-11.Vcc
  N3: U1.GND#6, U1.GND#13, U1.GND#16, U1.GND#33, 470uf.-, HLK-PM1.-Vo, 2N3904.E, 2N3904_2.E, HW-484.GND, DHT-11.GND_2
  N4: U1.D5, HW-484.AUD
  N5: U1.D6, DHT-11.Data-signal, R3.Pin_0
  N6: U1.Vin, 470uf.+, HLK-PM1.+Vo, 5v_relay.MAIN, diode.cathode
  N7: Power_supply.GND, HLK-PM1.AC#1, 5v_relay.COIL2
  N8: Power_supply.VCC, HLK-PM1.AC#0, Lamp_220v.C
  N9: R1.Pin_1, 2N3904.B
  N10: 5v_relay.NO, Lamp_220v.A
  N11: 5v_relay.NC, 2N3904.C
  N12: 2N3904_2.B, R2.Pin_1
  N13: 2N3904_2.C, part.cathode

notes:
  3.3v
  5v

custom parts:
  NodeMCU V3.0: ESP8266 based NodeMCU
