# Fritzing sketch rgb_led_with_pir (saved by Fritzing 0.9.3b)
breadboards: 1

parts:
  U1 = NodeMCU V3.0
  M1 = RioRand LM2596
  Power_plug1 = Power plug [part_number=12v]
  Q1 = Basic FET N-Channel [package="TO220 [THT]"]
  Q2 = Basic FET N-Channel [package="TO220 [THT]"]
  Q3 = Basic FET N-Channel [package="TO220 [THT]"]
  U2 = Tri-Color LED SMD [package=led-tricolor-smd]
  Lhi1 = LHi958 [package=to-39]

nets:
  N1: U1.D2, Lhi1.S
  GND: U1.GND#6, U1.GND#13, U1.GND#16, U1.GND#33, M1.Pin_2, M1.Pin_4, Power_plug1.GND, Q1.source, Q2.source, Q3.source, Lhi1.GND
  N2: U1.D5, Q1.gate
  N3: U1.D6, Q2.gate
  N4: U1.D7, Q3.gate
  N5: U1.Vin, M1.Pin_3, Lhi1.D
  N6: M1.Pin_1, Power_plug1.VCC, U2.A
  N7: Q1.drain, U2.RED
  N8: Q2.drain, U2.GRN
  N9: Q3.drain, U2.BLU

notes:
  12v
  5v
  RGB led strip 12v
  PIR

custom parts:
  NodeMCU V3.0: ESP8266 based NodeMCU
